// Logisim project n16.circ as structural Verilog: 7 circuits, main circuit main
module main (
  input  IRQ_0,
  input  IRQ_1,
  input  IRQ_2,
  input  IRQ_3,
  input  IRQ_4,
  input  IRQ_5,
  input  IRQ_6,
  input  IRQ_7,
  output [2:0] INT
);

  wire ALU_2, ALU_C, ALU_SRC_A, ALU_Z, CLK, EN_IR, EN_MDR, EN_PC_0, EN_RAM, PC_0_SRC, priority_encoder_1_gs,
       RAM_BYTE, RAM_LD, RAM_W, RU_EN_RT, RU_HI_REG, RU_SEL_RS, RU_SEL_RT, RU_SRC, SEL_ALU;
  wire [1:0] ALU_SRC_B, RAM_DAT_SRC;
  wire [2:0] RU_SRC_RS, RU_SRC_RT;
  wire [3:0] ALU_OP;
  wire [15:0] adder_1_out, ALU_OUT, multiplexer_1_out, multiplexer_2_out, multiplexer_3_out,
       multiplexer_4_out, multiplexer_5_out, PC_0_q, REGISTER_FILE_rs_data_out, REGISTER_FILE_rt_data_out,
       undriven;
  wire [15:10] IR_q;
  wire [31:0] RAM_D_IN, RAM_d_out;

  Clock clock_1 (.out(CLK));
  Adder #(.width(16)) adder_1 (.a(PC_0_q), .b(16'h2), .out(adder_1_out));  // open: cin, cout
  Multiplexer #(.width(16), .enable("false")) multiplexer_1 (
    .in0(adder_1_out), .in1(ALU_OUT), .out(multiplexer_1_out), .sel(PC_0_SRC));
  Register #(.width(16)) PC_0 (.D(multiplexer_1_out), .en(EN_PC_0), .Q(PC_0_q), .clk(CLK));  // open: clr
  // Probe on multiplexer_2_out
  Multiplexer #(.width(16), .enable("false")) multiplexer_2 (
    .in0(ALU_OUT), .out(multiplexer_2_out), .sel(RU_SRC));  // open: in1
  Multiplexer #(.select(2), .width(16), .enable("false")) multiplexer_3 (
    .in0(PC_0_q), .in1(ALU_OUT), .out(multiplexer_3_out), .sel(RAM_DAT_SRC));  // open: in2, in3
  // Probe on RAM_DAT_SRC
  Priority_Encoder priority_encoder_1 (
    .in0(IRQ_0), .in1(IRQ_1), .in2(IRQ_2), .in3(IRQ_3), .in4(IRQ_4), .in5(IRQ_5), .in6(IRQ_6), .in7(IRQ_7),
    .out(INT), .gs(priority_encoder_1_gs));  // open: en_in, en_out
  REGISTER_UNIT REGISTER_FILE (
    .RT_DATA_IN(multiplexer_2_out), .SEL_RS(RU_SEL_RS), .EN_RT(RU_EN_RT), .SRC_RT({RU_HI_REG, RU_SRC_RT}),
    .SRC_RS({RU_HI_REG, RU_SRC_RS}), .CLK(CLK), .SEL_RT(RU_SEL_RT), .RT_DATA_OUT(REGISTER_FILE_rt_data_out),
    .RS_DATA_OUT(REGISTER_FILE_rs_data_out));
  // Probe on {RU_HI_REG, RU_SRC_RS}
  // Probe on {RU_HI_REG, RU_SRC_RT}
  RAM RAM (
    .D_IN(RAM_D_IN), .RAM_W(RAM_W), .CLK(CLK), .ADDR({undriven, multiplexer_3_out}), .RAM_BYTE(RAM_BYTE),
    .SEL(RAM_LD), .D_OUT(RAM_d_out));
  Multiplexer #(.width(16), .enable("false")) multiplexer_4 (
    .in0(REGISTER_FILE_rt_data_out), .out(multiplexer_4_out), .sel(ALU_SRC_A));  // open: in1
  Multiplexer #(.select(2), .width(16), .enable("false")) multiplexer_5 (
    .in0(REGISTER_FILE_rs_data_out), .out(multiplexer_5_out), .sel(ALU_SRC_B));  // open: in1, in2, in3
  Register #(.width(16)) MDR (.D(RAM_d_out[15:0]), .en(EN_MDR), .clk(CLK));  // open: Q, clr
  Register #(.width(16)) IR (
    .D(RAM_d_out[15:0]), .en(EN_IR), .Q({IR_q, RU_SRC_RT, RU_SRC_RS, ALU_OP}), .clk(CLK));  // open: clr
  CONTROL CONTROL (
    .BUS_INST(RAM_d_out[15:10]), .CLK(CLK), .ALU_C(ALU_C), .ALU_Z(ALU_Z), .ALU_2(ALU_2),
    .IRQ(priority_encoder_1_gs), .out_12(EN_PC_0), .EN_IR_0(PC_0_SRC), .EN_IR_1(EN_IR), .PC_S_0(EN_MDR),
    .PC_S_1(RAM_DAT_SRC[0]), .EN_PC(RAM_DAT_SRC[1]), .EN_RAM(EN_RAM), .RAM_R(RAM_W), .out_20(RAM_LD),
    .out_21(RAM_BYTE), .out_22(RU_HI_REG), .out_23(RU_SRC), .out_24(RU_EN_RT), .out_25(RU_SEL_RT),
    .out_26(RU_SEL_RS), .out_27(RU_HI_REG), .out_28(ALU_SRC_A), .out_29(ALU_SRC_B[0]), .out_30(ALU_SRC_B[1]),
    .out_31(SEL_ALU));  // open: EN_INST, EN_MC_DEC, MC_DEC_0, MC_DEC_1, MC_DEC_2, out_32, out_33, out_34, out_35, out_36, out_37, out_38
  // Probe on multiplexer_4_out
  ALU ALU (
    .R_S(multiplexer_4_out), .R_T(multiplexer_5_out), .ALU_OP(ALU_OP), .SEL_ALU(SEL_ALU), .ALU_OUT(ALU_OUT),
    .Z(ALU_Z), .C(ALU_C), .N(ALU_2));
  // Probe on multiplexer_5_out
  // Probe on ALU_OUT
  // Probe on ALU_OP
  LED led_1 (.in(EN_PC_0));
  LED led_2 (.in(PC_0_SRC));
  LED led_3 (.in(EN_IR));
  LED led_4 (.in(EN_MDR));
  // Probe on RAM_DAT_SRC
  LED led_5 (.in(EN_RAM));
  LED led_6 (.in(RAM_W));
  LED led_7 (.in(RAM_LD));
  LED led_8 (.in(RAM_BYTE));
  LED led_9 (.in(RU_HI_REG));
  LED led_10 (.in(RU_SRC));
  LED led_11 (.in(RU_EN_RT));
  LED led_12 (.in(RU_SEL_RT));
  LED led_13 (.in(RU_SEL_RS));
  LED led_14 (.in(RU_HI_REG));
  LED led_15 (.in(ALU_SRC_A));
  // Probe on ALU_SRC_B
  LED led_16 (.in(SEL_ALU));

  // Other names for the same wires on the sheet: RU_SRC_RS[3] = RU_HI_REG; RU_SRC_RT[3] = RU_HI_REG
endmodule

module RAM (
  input  [31:0] D_IN,
  input  RAM_W,
  input  CLK,
  input  [31:0] ADDR,
  input  RAM_BYTE,
  input  SEL,
  output [31:0] D_OUT
);

  wire and_1_out, and_2_out, decoder_1_out0, decoder_1_out1, not_1_out, not_2_out;
  wire [7:0] demultiplexer_1_out0, multiplexer_1_out;
  wire [31:0] multiplexer_2_out;
  wire [31:8] demultiplexer_1_out1, undriven;

  Pull_Resistor pull_resistor_1 (.node(ADDR));
  not not_1 (not_1_out, RAM_BYTE);
  Decoder decoder_1 (.out0(decoder_1_out0), .out1(decoder_1_out1), .sel(ADDR[0]), .en(RAM_BYTE));
  and and_1 (and_1_out, not_1_out, RAM_W);
  not not_2 (not_2_out, RAM_W);
  Demultiplexer #(.width(8)) demultiplexer_1 (
    .out0(demultiplexer_1_out0), .out1(demultiplexer_1_out1[15:8]), .in(D_IN[7:0]), .sel(ADDR[0]),
    .en(and_2_out));
  and and_2 (and_2_out, RAM_BYTE, RAM_W);
  Pull_Resistor #(.pull(1)) pull_resistor_2 (.node(decoder_1_out0));
  Pull_Resistor #(.pull(1)) pull_resistor_3 (.node(decoder_1_out1));
  assign {demultiplexer_1_out1, demultiplexer_1_out0} = and_1_out ? D_IN : 32'bz;  // Controlled_Buffer controlled_buffer_1
  RAM_part #(.addrWidth(24)) ram_1 (
    .addr(ADDR[24:1]), .data(demultiplexer_1_out0), .sel(decoder_1_out0), .clk(CLK), .ld(not_2_out));  // open: clr
  RAM_part #(.addrWidth(24)) ram_2 (
    .addr(ADDR[24:1]), .data(demultiplexer_1_out1[15:8]), .sel(decoder_1_out1), .clk(CLK), .ld(not_2_out));  // open: clr
  Multiplexer #(.width(8), .enable("false")) multiplexer_1 (
    .in0(demultiplexer_1_out0), .in1(demultiplexer_1_out1[15:8]), .out(multiplexer_1_out));  // open: sel
  Multiplexer #(.width(32), .enable("false")) multiplexer_2 (
    .in0({demultiplexer_1_out1, demultiplexer_1_out0}), .in1({undriven, multiplexer_1_out}),
    .out(multiplexer_2_out), .sel(RAM_BYTE));
  assign D_OUT = SEL ? multiplexer_2_out : 32'bz;  // Controlled_Buffer controlled_buffer_2
endmodule

module CONTROL (
  input  [5:0] BUS_INST,
  input  CLK,
  input  ALU_C,
  input  ALU_Z,
  input  ALU_2,
  input  IRQ,
  output EN_INST,
  output EN_MC_DEC,
  output MC_DEC_0,
  output MC_DEC_1,
  output MC_DEC_2,
  output out_12,
  output EN_IR_0,
  output EN_IR_1,
  output PC_S_0,
  output PC_S_1,
  output EN_PC,
  output EN_RAM,
  output RAM_R,
  output out_20,
  output out_21,
  output out_22,
  output out_23,
  output out_24,
  output out_25,
  output out_26,
  output out_27,
  output out_28,
  output out_29,
  output out_30,
  output out_31,
  output out_32,
  output out_33,
  output out_34,
  output out_35,
  output out_36,
  output out_37,
  output out_38
);

  wire and_1_out, and_2_out, multiplexer_1_out, nCLK, not_2_out, not_3_out;
  wire [2:0] rom_2_data;
  wire [7:0] BUS_INST_t, register_1_q;

  not not_1 (nCLK, CLK);
  assign BUS_INST_t = not_2_out ? {BUS_INST, 2'b00} : 8'bz;  // Controlled_Buffer controlled_buffer_1
  not not_2 (not_2_out, EN_MC_DEC);
  Multiplexer #(.select(3), .enable("false")) multiplexer_1 (
    .in0(1'b1), .in1(ALU_C), .in2(ALU_Z), .in3(ALU_2), .in4(IRQ), .out(multiplexer_1_out),
    .sel({MC_DEC_2, MC_DEC_1, MC_DEC_0}));  // open: in5, in6, in7
  LED led_1 (.in(CLK));
  Register register_1 (.D(BUS_INST_t), .en(EN_INST), .Q(register_1_q), .clk(nCLK));  // open: clr
  and and_1 (and_1_out, multiplexer_1_out, EN_MC_DEC);
  and and_2 (and_2_out, not_3_out, EN_MC_DEC);
  not not_3 (not_3_out, multiplexer_1_out);
  ROM rom_1 (
    .addr(register_1_q), .data({EN_IR_1, EN_IR_0, out_12, MC_DEC_2, MC_DEC_1, MC_DEC_0, EN_MC_DEC, EN_INST}));  // open: sel
  ROM rom_2 (.addr(register_1_q), .data({out_22, out_21, out_20, RAM_R, EN_RAM, rom_2_data}));  // open: sel
  ROM rom_3 (
    .addr(register_1_q), .data({out_30, out_29, out_28, out_27, out_26, out_25, out_24, out_23}));  // open: sel
  ROM rom_4 (
    .addr(register_1_q), .data({out_38, out_37, out_36, out_35, out_34, out_33, out_32, out_31}));  // open: sel
  ROM rom_5 (.addr(register_1_q), .data(BUS_INST_t), .sel(and_1_out));
  ROM rom_6 (.addr(register_1_q), .data(BUS_INST_t), .sel(and_2_out));
  D_Flip_Flop d_ff_1 (.clk(CLK), .D(rom_2_data[0]), .Q(PC_S_0));  // open: Qn, preset, en, reset
  D_Flip_Flop d_ff_2 (.clk(CLK), .D(rom_2_data[1]), .Q(PC_S_1));  // open: Qn, preset, en, reset
  D_Flip_Flop d_ff_3 (.clk(CLK), .D(rom_2_data[2]), .Q(EN_PC));  // open: Qn, preset, en, reset
endmodule

module _3_STATE_REGISTER (
  input  [15:0] D,
  input  sel_s,
  input  en,
  input  clk,
  input  _0,
  input  sel_t,
  output [15:0] Q_S,
  output [15:0] Q_T
);

  wire [15:0] register_1_q;

  Register #(.width(16)) register_1 (.D(D), .en(en), .Q(register_1_q), .clk(clk), .clr(_0));
  assign Q_S = sel_s ? register_1_q : 16'bz;  // Controlled_Buffer controlled_buffer_1
  Pull_Resistor pull_resistor_1 (.node(sel_s));
  assign Q_T = sel_t ? register_1_q : 16'bz;  // Controlled_Buffer controlled_buffer_2
  Pull_Resistor pull_resistor_2 (.node(sel_t));
endmodule

module REGISTER_UNIT (
  input  [15:0] RT_DATA_IN,
  input  EN_RT,
  input  SEL_RT,
  input  [3:0] SRC_RT,
  input  CLK,
  input  [3:0] SRC_RS,
  input  SEL_RS,
  output [15:0] RT_DATA_OUT,
  output [15:0] RS_DATA_OUT
);

  wire decoder_1_out0, decoder_1_out1, decoder_1_out2, decoder_1_out3, decoder_1_out4, decoder_1_out5,
       decoder_1_out6, decoder_1_out7, decoder_1_out8, decoder_1_out9, decoder_1_out10, decoder_1_out11,
       decoder_1_out12, decoder_1_out13, decoder_1_out14, decoder_1_out15, decoder_2_out0, decoder_2_out1,
       decoder_2_out2, decoder_2_out3, decoder_2_out4, decoder_2_out5, decoder_2_out6, decoder_2_out7,
       decoder_2_out8, decoder_2_out9, decoder_2_out10, decoder_2_out11, decoder_2_out12, decoder_2_out13,
       decoder_2_out14, decoder_2_out15, decoder_3_out0, decoder_3_out1, decoder_3_out2, decoder_3_out3,
       decoder_3_out4, decoder_3_out5, decoder_3_out6, decoder_3_out7, decoder_3_out8, decoder_3_out9,
       decoder_3_out10, decoder_3_out11, decoder_3_out12, decoder_3_out13, decoder_3_out14, decoder_3_out15;
  wire [3:0] BUS_RT;

  Decoder #(.select(4)) decoder_1 (
    .out0(decoder_1_out0), .out1(decoder_1_out1), .out2(decoder_1_out2), .out3(decoder_1_out3),
    .out4(decoder_1_out4), .out5(decoder_1_out5), .out6(decoder_1_out6), .out7(decoder_1_out7),
    .out8(decoder_1_out8), .out9(decoder_1_out9), .out10(decoder_1_out10), .out11(decoder_1_out11),
    .out12(decoder_1_out12), .out13(decoder_1_out13), .out14(decoder_1_out14), .out15(decoder_1_out15),
    .sel(BUS_RT), .en(EN_RT));
  Decoder #(.select(4)) decoder_2 (
    .out0(decoder_2_out0), .out1(decoder_2_out1), .out2(decoder_2_out2), .out3(decoder_2_out3),
    .out4(decoder_2_out4), .out5(decoder_2_out5), .out6(decoder_2_out6), .out7(decoder_2_out7),
    .out8(decoder_2_out8), .out9(decoder_2_out9), .out10(decoder_2_out10), .out11(decoder_2_out11),
    .out12(decoder_2_out12), .out13(decoder_2_out13), .out14(decoder_2_out14), .out15(decoder_2_out15),
    .sel(SRC_RS), .en(SEL_RS));
  _3_STATE_REGISTER u_3_state_register_1 (
    .D(RT_DATA_IN), .en(decoder_1_out0), .clk(CLK), .sel_s(decoder_2_out0), .sel_t(decoder_3_out0),
    .Q_S(RS_DATA_OUT), .Q_T(RT_DATA_OUT));  // open: _0
  _3_STATE_REGISTER u_3_state_register_2 (
    .D(RT_DATA_IN), .en(decoder_1_out4), .clk(CLK), .sel_s(decoder_2_out4), .sel_t(decoder_3_out4),
    .Q_S(RS_DATA_OUT), .Q_T(RT_DATA_OUT));  // open: _0
  _3_STATE_REGISTER u_3_state_register_3 (
    .D(RT_DATA_IN), .en(decoder_1_out8), .clk(CLK), .sel_s(decoder_2_out8), .sel_t(decoder_3_out8),
    .Q_S(RS_DATA_OUT), .Q_T(RT_DATA_OUT));  // open: _0
  _3_STATE_REGISTER u_3_state_register_4 (
    .D(RT_DATA_IN), .en(decoder_1_out12), .clk(CLK), .sel_s(decoder_2_out12), .sel_t(decoder_3_out12),
    .Q_S(RS_DATA_OUT), .Q_T(RT_DATA_OUT));  // open: _0
  _3_STATE_REGISTER u_3_state_register_5 (
    .D(RT_DATA_IN), .en(decoder_1_out1), .clk(CLK), .sel_s(decoder_2_out1), .sel_t(decoder_3_out1),
    .Q_S(RS_DATA_OUT), .Q_T(RT_DATA_OUT));  // open: _0
  _3_STATE_REGISTER u_3_state_register_6 (
    .D(RT_DATA_IN), .en(decoder_1_out5), .clk(CLK), .sel_s(decoder_2_out5), .sel_t(decoder_3_out5),
    .Q_S(RS_DATA_OUT), .Q_T(RT_DATA_OUT));  // open: _0
  _3_STATE_REGISTER u_3_state_register_7 (
    .D(RT_DATA_IN), .en(decoder_1_out9), .clk(CLK), .sel_s(decoder_2_out9), .sel_t(decoder_3_out9),
    .Q_S(RS_DATA_OUT), .Q_T(RT_DATA_OUT));  // open: _0
  _3_STATE_REGISTER u_3_state_register_8 (
    .D(RT_DATA_IN), .en(decoder_1_out13), .clk(CLK), .sel_s(decoder_2_out13), .sel_t(decoder_3_out13),
    .Q_S(RS_DATA_OUT), .Q_T(RT_DATA_OUT));  // open: _0
  _3_STATE_REGISTER u_3_state_register_9 (
    .D(RT_DATA_IN), .en(decoder_1_out2), .clk(CLK), .sel_s(decoder_2_out2), .sel_t(decoder_3_out2),
    .Q_S(RS_DATA_OUT), .Q_T(RT_DATA_OUT));  // open: _0
  _3_STATE_REGISTER u_3_state_register_10 (
    .D(RT_DATA_IN), .en(decoder_1_out6), .clk(CLK), .sel_s(decoder_2_out6), .sel_t(decoder_3_out6),
    .Q_S(RS_DATA_OUT), .Q_T(RT_DATA_OUT));  // open: _0
  _3_STATE_REGISTER u_3_state_register_11 (
    .D(RT_DATA_IN), .en(decoder_1_out10), .clk(CLK), .sel_s(decoder_2_out10), .sel_t(decoder_3_out10),
    .Q_S(RS_DATA_OUT), .Q_T(RT_DATA_OUT));  // open: _0
  _3_STATE_REGISTER u_3_state_register_12 (
    .D(RT_DATA_IN), .en(decoder_1_out14), .clk(CLK), .sel_s(decoder_2_out14), .sel_t(decoder_3_out14),
    .Q_S(RS_DATA_OUT), .Q_T(RT_DATA_OUT));  // open: _0
  _3_STATE_REGISTER u_3_state_register_13 (
    .D(RT_DATA_IN), .en(decoder_1_out3), .clk(CLK), .sel_s(decoder_2_out3), .sel_t(decoder_3_out3),
    .Q_S(RS_DATA_OUT), .Q_T(RT_DATA_OUT));  // open: _0
  _3_STATE_REGISTER u_3_state_register_14 (
    .D(RT_DATA_IN), .en(decoder_1_out7), .clk(CLK), .sel_s(decoder_2_out7), .sel_t(decoder_3_out7),
    .Q_S(RS_DATA_OUT), .Q_T(RT_DATA_OUT));  // open: _0
  _3_STATE_REGISTER u_3_state_register_15 (
    .D(RT_DATA_IN), .en(decoder_1_out11), .clk(CLK), .sel_s(decoder_2_out11), .sel_t(decoder_3_out11),
    .Q_S(RS_DATA_OUT), .Q_T(RT_DATA_OUT));  // open: _0
  _3_STATE_REGISTER u_3_state_register_16 (
    .D(RT_DATA_IN), .en(decoder_1_out15), .clk(CLK), .sel_s(decoder_2_out15), .sel_t(decoder_3_out15),
    .Q_S(RS_DATA_OUT), .Q_T(RT_DATA_OUT));  // open: _0
  Decoder #(.select(4)) decoder_3 (
    .out0(decoder_3_out0), .out1(decoder_3_out1), .out2(decoder_3_out2), .out3(decoder_3_out3),
    .out4(decoder_3_out4), .out5(decoder_3_out5), .out6(decoder_3_out6), .out7(decoder_3_out7),
    .out8(decoder_3_out8), .out9(decoder_3_out9), .out10(decoder_3_out10), .out11(decoder_3_out11),
    .out12(decoder_3_out12), .out13(decoder_3_out13), .out14(decoder_3_out14), .out15(decoder_3_out15),
    .sel(SRC_RT), .en(SEL_RT));
endmodule

module ALU (
  input  [15:0] R_S,
  input  [15:0] R_T,
  input  [3:0] ALU_OP,
  input  SEL_ALU,
  output [15:0] ALU_OUT,
  output Z,
  output C,
  output N
);

  wire [15:0] adder_1_out, multiplier_1_out, subtractor_1_out;

  Adder #(.width(16)) adder_1 (.a(R_S), .b(R_T), .out(adder_1_out));  // open: cin, cout
  Subtractor #(.width(16)) subtractor_1 (.a(R_S), .b(R_T), .out(subtractor_1_out));  // open: bin, bout
  Multiplier #(.width(16)) multiplier_1 (.a(R_S), .b(R_T), .out(multiplier_1_out));  // open: cin, cout
  Multiplexer #(.select(4), .width(16)) multiplexer_1 (
    .in6(R_S), .in7(adder_1_out), .in8(subtractor_1_out), .in9(multiplier_1_out), .out(ALU_OUT),
    .sel(ALU_OP), .en(SEL_ALU));  // open: in0, in1, in2, in3, in4, in5, in10, in11, in12, in13, in14, in15
  Pull_Resistor pull_resistor_1 (.node(C));

  assign N = C;
  assign Z = C;
endmodule

module ALGN_SIGN_EXT_26_32 (
  input  [9:0] IN,
  output [31:0] OUT
);


  assign OUT = {{22{IN[9]}}, IN[8:0], 1'b0};
endmodule
